# Fritzing sketch wiringdiagram (saved by Fritzing 0.9.3b)
breadboards: 1

parts:
  Part1 = Arduino Uno (Rev3)
  R1 = Resistor [tolerance=±5% resistance=330 package="0402 [SMD]"]
  R2 = Resistor [tolerance=±5% resistance=330 package="0402 [SMD]"]
  R3 = Resistor [tolerance=±5% resistance=330 package="0402 [SMD]"]
  hc-sr1 = hc-sr04
  LED1 = RGB LED (com. cathode, rgb) [package="5 mm [THT]"]

nets:
  N1: Part1.D9_PWM, R3.Pin_1
  N2: Part1.D10_PWM/SS, R2.Pin_1
  N3: Part1.D11_PWM/MOSI, R1.Pin_1
  N4: Part1.D5_PWM, hc-sr1.Trig
  N5: Part1.D6_PWM, hc-sr1.Echo
  5V: Part1.5V, hc-sr1.VCC, LED1.common_cathode
  GND: Part1.GND, hc-sr1.GND
  N6: R1.Pin_0, LED1.blue_anode
  N7: R2.Pin_0, LED1.green_anode
  N8: R3.Pin_0, LED1.red_anode
